// Logisim project sdp16_blink_intr.circ as structural Verilog: 1 circuit, main circuit main
module main (
  input  [7:0] in_1,
  input  [3:0] in_2,
  input  RUN___STEP
);

  wire and_1_out, and_2_out, and_3_out, button_1_out, button_2_out, button_3_out, clock_1_out, clock_2_out,
       d_ff_1_p3, d_ff_1_p6, d_ff_2_p4, decoder_1_out0, decoder_1_out1, decoder_1_out2, decoder_1_out3,
       NEXT_out, not_1_out, p16_1_p1, p16_1_p7, p16_1_p10, p16_1_p11, p16_1_p12, p16_1_p13, p16_1_p14,
       p16_1_p15, p16_1_p16, p16_1_p17;
  wire [7:0] register_2_q, undriven;
  wire [15:0] p16_1_p9, register_1_q;

  Clock clock_1 (.out(clock_1_out));
  Button button_1 (.out(button_1_out));
  Button button_2 (.out(button_2_out));
  not not_1 (not_1_out, button_1_out);
  Button NEXT (.out(NEXT_out));
  Clock #(.highDuration(500), .lowDuration(500)) clock_2 (.out(clock_2_out));
  // Probe on nothing
  // Probe on nothing
  // Probe on nothing
  // Probe on nothing
  // P16 p16_1: pin names not known; wires that end beside it: p16_1_p1, not_1_out, in_1, button_2_out, in_2, clock_1_out, p16_1_p7, 1'b0, p16_1_p9, p16_1_p10, p16_1_p11, p16_1_p12, p16_1_p13, p16_1_p14, p16_1_p15, p16_1_p16, p16_1_p17, p16_1_p11, p16_1_p12, p16_1_p13, p16_1_p14, 1'b1, register_1_q[15]
  // D_Flip_Flop d_ff_1: pin names not known; wires that end beside it: 1'b1, NEXT_out, d_ff_1_p3, RUN___STEP, d_ff_1_p3, d_ff_1_p6, p16_1_p7
  // D_Flip_Flop d_ff_2: pin names not known; wires that end beside it: 1'b1, clock_2_out, 1'b1, d_ff_2_p4, p16_1_p1
  Register #(.width(16), .trigger("high")) register_1 (
    .D(p16_1_p9), .en(1'b1), .Q(register_1_q), .clk(p16_1_p10), .clr(1'b0));
  not not_2 (d_ff_1_p6, p16_1_p10);
  // Probe on register_1_q
  nand nand_1 (d_ff_2_p4, ~p16_1_p15, decoder_1_out1);  // NAND_Gate
  and and_1 (and_1_out, register_1_q[8], register_1_q[9], register_1_q[10], register_1_q[11], register_1_q[12], register_1_q[13], register_1_q[14], register_1_q[15]);
  // Probe on p16_1_p9[15:8]
  RAM #(.addrWidth(14)) ram_1 (.addr(register_1_q[14:1]), .data(p16_1_p9[15:8]));  // open: sel, clk, ld, clr
  Decoder #(.select(2), .disabled(0)) decoder_1 (
    .out0(decoder_1_out0), .out1(decoder_1_out1), .out2(decoder_1_out2), .out3(decoder_1_out3),
    .sel(register_1_q[7:6]), .en(and_1_out));
  not not_3 (undriven[3], button_3_out);
  Button button_3 (.out(button_3_out));
  // Probe on p16_1_p9[7:0]
  and and_2 (and_2_out, ~p16_1_p15, decoder_1_out0);  // AND_Gate
  and and_3 (and_3_out, ~p16_1_p17, decoder_1_out0);  // AND_Gate
  assign p16_1_p9[7:0] = and_2_out ? undriven : 8'bz;  // Controlled_Buffer controlled_buffer_1
  RAM #(.addrWidth(14)) ram_2 (.addr(register_1_q[14:1]), .data(p16_1_p9[7:0]));  // open: sel, clk, ld, clr
  Register #(.trigger("high")) register_2 (.D(p16_1_p9[7:0]), .en(1'b1), .Q(register_2_q), .clk(and_3_out), .clr(1'b0));
  LED led_1 (.in(register_2_q[0]));
endmodule
